# Fritzing sketch Electronic sketch (saved by Fritzing 0.9.3b)
breadboards: 1

parts:
  Part1 = Arduino Uno (Rev3) - ICSP
  Mod1 = L298N DC motor driver
  Part2 = Bluetooth HC-05 Macho
  Mod2 = L298N DC motor driver
  M2 = DC Motor
  M3 = DC Motor
  M4 = DC Motor
  M5 = DC Motor
  U1 = BATTERY-2 [package=battery-aaa]

nets:
  N1: Part1.D9_PWM, Mod1.ENA
  N2: Part1.D10_PWM/SS, Mod2.ENA
  N3: Part1.D11_PWM/MOSI, Mod2.ENB
  GND: Part1.GND, Mod1.GND, Part2.GND, Mod2.GND, U1.+1
  N4: Part1.D0/RX, Part2.TXD
  N5: Part1.D1/TX, Part2.RXD
  N6: Part1.D2, Mod1.IN2
  N7: Part1.D3_PWM, Mod1.IN1
  N8: Part1.D4, Mod2.IN2
  N9: Part1.D5_PWM, Mod2.IN1
  N10: Part1.D6_PWM, Mod2.IN3
  N11: Part1.D7, Mod2.IN4
  5V: Part1.5V, Part2.VCC
  VIN: Part1.VIN, Mod1.5V, Mod1.+5V-J1
  N12: Mod1.OUT1, M2.pin_2, M5.pin_2
  N13: Mod1.OUT2, M2.pin_1, M5.pin_1
  12V: Mod1.12V, Mod1.5V-ENA-JMP-I, Mod1.5V-ENA-JMP-O, Mod2.12V, Mod2.5V-ENA-JMP-I, U1.-1
  N14: Mod2.OUT1, M3.pin_2
  N15: Mod2.OUT2, M3.pin_1
  N16: Mod2.OUT3, M4.pin_2
  N17: Mod2.OUT4, M4.pin_1

custom parts:
  L298N DC motor driver: 2x DC motor driver with 78M05 positive voltage regulator (7..35 V) L298N: max 46 V, 2 A Set 5 V Enable jumper to enable 5 V regultor (needed for the L298N) and +5 V output at screw terminal or supply external +5 V at screw terminal Set ENA and/or ENB to +5 V to enable motor permanently or supply ENA and/or ENB with PWM signal IN1 and IN2 set rotation directory for motor A (OUT1/OUT2) IN2 and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
